// Logisim project mips.circ as structural Verilog: 16 circuits, main circuit MIPS
module MIPS (
);

  wire and_2_out, and_4_out, and_7_out, and_16_out, and_19_out, and_20_out, and_21_out, and_22_out,
       and_23_out, and_24_out, and_25_out, and_26_out, and_27_out, branchyes_1_out_5, Clk_out,
       decode_1_instr_is_branch_or_jump, decode_1_load, decode_1_store, decode_1_we, execute_1_weout,
       ExMemRs_out_3, ExMemRt_out_3, Load_q, MemWbRs_out_3, MemWbRt_out_3, not_1_out, not_2_out, not_3_out,
       not_4_out, not_5_out, not_6_out, not_7_out, not_8_out, rdequals0_1_out_3, rdequals0_2_out_3,
       rdequals0_3_out_3, register_3_q, register_7_q, register_8_q, register_9_q, registerfile_1_p3,
       stall_1_stall, Store_q, WE_q;
  wire [1:0] and_17_out, bit_extender_7_out, bit_extender_9_out, bit_extender_10_out, decode_1_pcsel,
       multiplexer_5_out, PCsel_q;
  wire [3:0] alu_op_q, and_1_out, and_12_out, bit_extender_5_out, decode_1_alu_opcode, decode_1_sel,
       multiplexer_12_out, onehot_1_out_2, register_10_q, sel_q;
  wire [4:0] and_6_out, and_9_out, and_10_out, and_14_out, bit_extender_3_out, bit_extender_8_out,
       decode_1_destination, decode_1_shamt, execute_1_regdst, rd_q, register_5_q, registerfile_1_p4,
       registerfile_1_p5, registerfile_1_p6, rs_q, rt_q, shamt_q;
  wire [5:0] and_3_out, and_11_out, bit_extender_4_out, ctrl_func_q, decode_1_ctrl_func, decode_1_firstsix,
       firstSix_q, firstSixD_q;
  wire [7:0] multiplexer_13_out;
  wire [25:0] and_15_out, bit_extender_6_out, decode_1_target, register_4_q;
  wire [29:0] incrementer_1_p1, incrementer_2_p1, incrementer_3_p2;
  wire [31:0] A_q, adder_1_out, and_5_out, and_8_out, and_13_out, and_18_out, B_q, bit_extender_1_out,
       bit_extender_2_out, bit_extender_11_out, bit_extender_12_out, decode_1_imm, execute_1_d, imm_q,
       leftshift2_1_out_3, mips_ram_1_p7, mipsprogramrom_1_p2, multiplexer_1_out, multiplexer_2_out,
       multiplexer_3_out, multiplexer_4_out, multiplexer_6_out, multiplexer_7_out, multiplexer_8_out,
       multiplexer_9_out, multiplexer_10_out, multiplexer_11_out, multiplexer_14_out, multiplexer_15_out,
       multiplexer_16_out, PC_q, PCFetch_q, register_1_q, register_2_q, register_6_q, register_11_q,
       registerfile_1_p1, registerfile_1_p7, registerfile_1_p8, shiftmultiple_1_out_5;
  wire [31:2] incrementer_1_p2;

  Clock Clk (.out(Clk_out));
  Multiplexer #(.select(2), .width(32), .enable("false")) multiplexer_1 (
    .in0(register_1_q), .in1(multiplexer_8_out), .in2({PC_q[31:28], register_4_q, bit_extender_10_out}),
    .in3(multiplexer_11_out), .out(multiplexer_1_out), .sel(PCsel_q));
  Multiplexer #(.width(32), .enable("false")) multiplexer_2 (
    .in0({incrementer_1_p2, multiplexer_5_out}), .in1({incrementer_1_p1, multiplexer_5_out}),
    .out(multiplexer_2_out), .sel(stall_1_stall));
  // Incrementer #(.width(30)) incrementer_1: pin names not known; wires that end beside it: incrementer_1_p1, incrementer_1_p2
  // MIPSProgramROM mipsprogramrom_1: pin names not known; wires that end beside it: multiplexer_1_out, mipsprogramrom_1_p2
  Register #(.width(32)) register_1 (
    .D(multiplexer_3_out), .en(not_1_out), .clk(Clk_out), .Q(register_1_q));  // open: clr
  Multiplexer #(.width(32), .enable("false")) multiplexer_3 (
    .in0(multiplexer_2_out), .in1({incrementer_1_p1, multiplexer_5_out}), .out(multiplexer_3_out),
    .sel(and_27_out));
  not not_1 (not_1_out, stall_1_stall);
  assign bit_extender_1_out = {{31{1'b0}}, mipsprogramrom_1_p2[30]};  // Bit_Extender bit_extender_1
  Register #(.width(32)) register_2 (.D(multiplexer_4_out), .clk(Clk_out), .Q(register_2_q));  // open: en, clr
  Multiplexer #(.width(32), .enable("false")) multiplexer_4 (
    .in0(mipsprogramrom_1_p2), .in1(bit_extender_1_out), .out(multiplexer_4_out), .sel(and_27_out));
  Multiplexer #(.width(32), .enable("false")) multiplexer_5 (
    .in0(register_1_q), .in1(multiplexer_1_out), .out({incrementer_1_p1, multiplexer_5_out}), .sel(and_27_out));
  Register #(.width(32)) PCFetch (
    .D({incrementer_1_p2, multiplexer_5_out}), .clk(Clk_out), .Q(PCFetch_q));  // open: en, clr
  // RegisterFile #(.trigger("falling")) registerfile_1: pin names not known; wires that end beside it: registerfile_1_p1, Clk_out, registerfile_1_p3, registerfile_1_p4, registerfile_1_p5, registerfile_1_p6, registerfile_1_p7, registerfile_1_p8
  Decode decode_1 (
    .Inst(register_2_q), .Destination(decode_1_destination), .Shamt(decode_1_shamt),
    .Ctrl_Func(decode_1_ctrl_func), .ALU_opCode(decode_1_alu_opcode), .Imm(decode_1_imm),
    .rS(registerfile_1_p5), .rT(registerfile_1_p6), .WE(decode_1_we), .firstSix(decode_1_firstsix),
    .Store(decode_1_store), .Load(decode_1_load), .sel(decode_1_sel),
    .instr_is_branch_or_jump(decode_1_instr_is_branch_or_jump), .PCsel(decode_1_pcsel),
    .target(decode_1_target));
  not not_2 (not_2_out, stall_1_stall);
  assign bit_extender_2_out = {{31{not_2_out}}, not_2_out};  // Bit_Extender bit_extender_2
  assign bit_extender_3_out = {{4{not_2_out}}, not_2_out};  // Bit_Extender bit_extender_3
  assign bit_extender_4_out = {{5{not_2_out}}, not_2_out};  // Bit_Extender bit_extender_4
  assign bit_extender_5_out = {{3{not_2_out}}, not_2_out};  // Bit_Extender bit_extender_5
  not not_3 (not_3_out, stall_1_stall);
  stall stall_1 (
    .load(decode_1_load), .rs(registerfile_1_p5), .rt(registerfile_1_p6), .rdNext(rd_q), .stall(stall_1_stall));
  assign bit_extender_6_out = {{25{not_3_out}}, not_3_out};  // Bit_Extender bit_extender_6
  assign and_1_out = decode_1_sel & bit_extender_5_out;  // AND_Gate and_1, 4 bits wide
  Register #(.width(1)) WE (.D(and_2_out), .clk(Clk_out), .Q(WE_q));  // open: en, clr
  and and_2 (and_2_out, decode_1_we, not_2_out);
  assign and_3_out = decode_1_firstsix & bit_extender_4_out;  // AND_Gate and_3, 6 bits wide
  and and_4 (and_4_out, decode_1_store, not_3_out);
  assign bit_extender_7_out = {{1{not_3_out}}, not_3_out};  // Bit_Extender bit_extender_7
  assign and_5_out = registerfile_1_p8 & bit_extender_2_out;  // AND_Gate and_5, 32 bits wide
  Register #(.width(32)) B (.D(and_5_out), .clk(Clk_out), .Q(B_q));  // open: en, clr
  Register #(.width(5)) rt (.D(and_6_out), .clk(Clk_out), .Q(rt_q));  // open: en, clr
  assign and_6_out = registerfile_1_p6 & bit_extender_3_out;  // AND_Gate and_6, 5 bits wide
  Register #(.width(6)) firstSixD (.D(and_3_out), .clk(Clk_out), .Q(firstSixD_q));  // open: en, clr
  Register #(.width(1)) Store (.D(and_4_out), .clk(Clk_out), .Q(Store_q));  // open: en, clr
  Register #(.width(1)) Load (.D(and_7_out), .clk(Clk_out), .Q(Load_q));  // open: en, clr
  and and_7 (and_7_out, decode_1_load, not_3_out);
  Register #(.width(4)) sel (.D(and_1_out), .clk(Clk_out), .Q(sel_q));  // open: en, clr
  assign and_8_out = registerfile_1_p7 & bit_extender_2_out;  // AND_Gate and_8, 32 bits wide
  Register #(.width(32)) A (.D(and_8_out), .clk(Clk_out), .Q(A_q));  // open: en, clr
  Register #(.width(5)) rd (.D(and_9_out), .clk(Clk_out), .Q(rd_q));  // open: en, clr
  assign and_9_out = decode_1_destination & bit_extender_3_out;  // AND_Gate and_9, 5 bits wide
  Register #(.width(5)) shamt (.D(and_10_out), .clk(Clk_out), .Q(shamt_q));  // open: en, clr
  assign and_10_out = decode_1_shamt & bit_extender_3_out;  // AND_Gate and_10, 5 bits wide
  Register #(.width(6)) ctrl_func (.D(and_11_out), .clk(Clk_out), .Q(ctrl_func_q));  // open: en, clr
  assign and_11_out = decode_1_ctrl_func & bit_extender_4_out;  // AND_Gate and_11, 6 bits wide
  Register #(.width(4)) alu_op (.D(and_12_out), .clk(Clk_out), .Q(alu_op_q));  // open: en, clr
  assign and_12_out = decode_1_alu_opcode & bit_extender_5_out;  // AND_Gate and_12, 4 bits wide
  Register #(.width(32)) imm (.D(and_13_out), .clk(Clk_out), .Q(imm_q));  // open: en, clr
  assign and_13_out = decode_1_imm & bit_extender_2_out;  // AND_Gate and_13, 32 bits wide
  Register #(.width(5)) rs (.D(and_14_out), .clk(Clk_out), .Q(rs_q));  // open: en, clr
  assign and_14_out = registerfile_1_p5 & bit_extender_3_out;  // AND_Gate and_14, 5 bits wide
  assign and_15_out = decode_1_target & bit_extender_6_out;  // AND_Gate and_15, 26 bits wide
  and and_16 (and_16_out, decode_1_instr_is_branch_or_jump, not_3_out);
  assign and_17_out = decode_1_pcsel & bit_extender_7_out;  // AND_Gate and_17, 2 bits wide
  AddressEquals ExMemRs (.A(register_5_q), .B(rs_q), .out_3(ExMemRs_out_3));
  AddressEquals ExMemRt (.A(register_5_q), .B(rt_q), .out_3(ExMemRt_out_3));
  assign bit_extender_8_out = {{4{1'b0}}, firstSixD_q[4]};  // Bit_Extender bit_extender_8
  Register #(.width(32)) PC (.D(and_18_out), .clk(Clk_out), .Q(PC_q));  // open: en, clr
  assign and_18_out = bit_extender_2_out & PCFetch_q;  // AND_Gate and_18, 32 bits wide
  Register #(.width(1)) register_3 (.D(and_16_out), .clk(Clk_out), .Q(register_3_q));  // open: en, clr
  Register #(.width(2)) PCsel (.D(and_17_out), .clk(Clk_out), .Q(PCsel_q));  // open: en, clr
  assign bit_extender_9_out = {{1{1'b0}}, firstSixD_q[4]};  // Bit_Extender bit_extender_9
  Register #(.width(26)) register_4 (.D(and_15_out), .clk(Clk_out), .Q(register_4_q));  // open: en, clr
  AddressEquals MemWbRs (.A(registerfile_1_p4), .B(rs_q), .out_3(MemWbRs_out_3));
  AddressEquals MemWbRt (.A(registerfile_1_p4), .B(rt_q), .out_3(MemWbRt_out_3));
  and and_19 (and_19_out, register_7_q, ExMemRs_out_3);
  and and_20 (and_20_out, ExMemRt_out_3, register_7_q);
  RdEquals0 rdequals0_1 (.Rd(register_5_q), .in_2(bit_extender_8_out), .out_3(rdequals0_1_out_3));
  RdEquals0 rdequals0_2 (.Rd(bit_extender_8_out), .in_2(registerfile_1_p4), .out_3(rdequals0_2_out_3));
  assign bit_extender_10_out = {{1{1'b0}}, firstSixD_q[4]};  // Bit_Extender bit_extender_10
  not not_4 (not_4_out, rdequals0_1_out_3);
  and and_21 (and_21_out, registerfile_1_p3, not_5_out);
  not not_5 (not_5_out, rdequals0_2_out_3);
  // Incrementer #(.width(30)) incrementer_2: pin names not known; wires that end beside it: incrementer_2_p1
  LeftShift2 leftshift2_1 (.in_1(imm_q), .in_2(bit_extender_9_out), .out_3(leftshift2_1_out_3));
  and and_22 (and_22_out, not_4_out, and_19_out);
  RdEquals0 rdequals0_3 (.Rd(registerfile_1_p4), .in_2(bit_extender_8_out), .out_3(rdequals0_3_out_3));
  not not_6 (not_6_out, rdequals0_3_out_3);
  and and_23 (and_23_out, and_20_out, not_4_out);
  not not_7 (not_7_out, and_22_out);
  and and_24 (and_24_out, registerfile_1_p3, not_6_out);
  not not_8 (not_8_out, and_23_out);
  and and_25 (and_25_out, and_21_out, not_8_out, MemWbRt_out_3);
  Adder #(.width(32)) adder_1 (.a(PC_q), .b(leftshift2_1_out_3), .out(adder_1_out));  // open: cin, cout
  Multiplexer #(.width(32), .enable("false")) multiplexer_6 (
    .in0(A_q), .in1(register_6_q), .out(multiplexer_6_out), .sel(and_22_out));
  and and_26 (and_26_out, and_24_out, not_7_out, MemWbRs_out_3);
  Multiplexer #(.width(32), .enable("false")) multiplexer_7 (
    .in0(B_q), .in1(register_6_q), .out(multiplexer_7_out), .sel(and_23_out));
  Multiplexer #(.width(32), .enable("false")) multiplexer_8 (
    .in0(multiplexer_6_out), .in1(registerfile_1_p1), .out(multiplexer_8_out), .sel(and_26_out));
  Multiplexer #(.width(32), .enable("false")) multiplexer_9 (
    .in0(multiplexer_7_out), .in1(registerfile_1_p1), .out(multiplexer_9_out), .sel(and_25_out));
  branchYes branchyes_1 (
    .A(multiplexer_8_out), .B(multiplexer_9_out), .firstSix(firstSixD_q), .rt(rt_q), .out_5(branchyes_1_out_5));
  and and_27 (and_27_out, branchyes_1_out_5, register_3_q);
  // Incrementer #(.width(30)) incrementer_3: pin names not known; wires that end beside it: PC_q[31:2], incrementer_3_p2
  Multiplexer #(.width(32), .enable("false")) multiplexer_10 (
    .in0(execute_1_d), .in1({incrementer_2_p1, PC_q[1:0]}), .out(multiplexer_10_out), .sel(register_3_q));
  Multiplexer #(.width(32), .enable("false")) multiplexer_11 (
    .in0({incrementer_3_p2, PC_q[1:0]}), .in1(adder_1_out), .out(multiplexer_11_out), .sel(and_27_out));
  Execute execute_1 (
    .Destination(rd_q), .A(multiplexer_8_out), .B(multiplexer_9_out), .Imm(imm_q), .Shamt(shamt_q),
    .Ctrl_Func(ctrl_func_q), .ALU_opCode(alu_op_q), .firstSix(firstSixD_q), .WEin(WE_q),
    .RegDst(execute_1_regdst), .D(execute_1_d), .WEout(execute_1_weout));
  Register #(.width(5)) register_5 (.D(execute_1_regdst), .clk(Clk_out), .Q(register_5_q));  // open: en, clr
  Register #(.width(32)) register_6 (.D(multiplexer_10_out), .clk(Clk_out), .Q(register_6_q));  // open: en, clr
  Register #(.width(1)) register_7 (.D(execute_1_weout), .clk(Clk_out), .Q(register_7_q));  // open: en, clr
  Register #(.width(1)) register_8 (.D(Store_q), .clk(Clk_out), .Q(register_8_q));  // open: en, clr
  Register #(.width(1)) register_9 (.D(Load_q), .clk(Clk_out), .Q(register_9_q));  // open: en, clr
  Register #(.width(4)) register_10 (.D(sel_q), .clk(Clk_out), .Q(register_10_q));  // open: en, clr
  Register #(.width(32)) register_11 (.D(B_q), .clk(Clk_out), .Q(register_11_q));  // open: en, clr
  Register #(.width(6)) firstSix (.D(firstSixD_q), .clk(Clk_out), .Q(firstSix_q));  // open: en, clr
  shiftMultiple shiftmultiple_1 (
    .in_1(register_11_q), .in_2(register_6_q[1:0]), .in_3(firstSix_q[4]), .in_4(firstSix_q[4]),
    .out_5(shiftmultiple_1_out_5));
  oneHot onehot_1 (.in_1(register_6_q[1:0]), .out_2(onehot_1_out_2));
  Multiplexer #(.width(4), .enable("false")) multiplexer_12 (
    .in0(onehot_1_out_2), .in1(register_10_q), .out(multiplexer_12_out), .sel(firstSix_q[0]));
  // MIPS_RAM #(.addrWidth(24)) mips_ram_1: pin names not known; wires that end beside it: register_6_q[25:2], shiftmultiple_1_out_5, register_8_q, multiplexer_12_out, Clk_out, register_9_q, mips_ram_1_p7
  Multiplexer #(.select(2), .width(8), .enable("false")) multiplexer_13 (
    .in0(mips_ram_1_p7[7:0]), .in1(mips_ram_1_p7[15:8]), .in2(mips_ram_1_p7[23:16]),
    .in3(mips_ram_1_p7[31:24]), .out(multiplexer_13_out), .sel(register_6_q[1:0]));
  assign bit_extender_11_out = {{24{multiplexer_13_out[7]}}, multiplexer_13_out};  // Bit_Extender bit_extender_11
  assign bit_extender_12_out = {{24{1'b0}}, multiplexer_13_out};  // Bit_Extender bit_extender_12
  Multiplexer #(.width(32), .enable("false")) multiplexer_14 (
    .in0(bit_extender_11_out), .in1(bit_extender_12_out), .out(multiplexer_14_out), .sel(firstSix_q[2]));
  Multiplexer #(.width(32), .enable("false")) multiplexer_15 (
    .in0(multiplexer_14_out), .in1(mips_ram_1_p7), .out(multiplexer_15_out), .sel(firstSix_q[0]));
  Register #(.width(5)) register_12 (.D(register_5_q), .clk(Clk_out), .Q(registerfile_1_p4));  // open: en, clr
  Register #(.width(32)) register_13 (.D(multiplexer_16_out), .clk(Clk_out), .Q(registerfile_1_p1));  // open: en, clr
  Multiplexer #(.width(32), .enable("false")) multiplexer_16 (
    .in0(register_6_q), .in1(multiplexer_15_out), .out(multiplexer_16_out), .sel(firstSix_q[5]));
  Register #(.width(1)) register_14 (.D(register_7_q), .clk(Clk_out), .Q(registerfile_1_p3));  // open: en, clr
  // AND_Gate and_28 is placed but not wired

  // Notes on the sheet:
  //   contents of mipsprogramrom_1 (hex, n*v repeats v):
  //   ADDIU $a0, $0, 5 ADDIU $a1, $0, 0x100 ADDIU $a2, $0, 50 ADDIU $sp, $0, 0x1000 jal fn nop j exit nop
  //   fn: nop  #prologue ADDIU $sp, $sp, -32 SW $ra, 28($sp) nop SW $fp, 24($sp) nop SW $a0, 4($sp) nop SW
  //   $a1, 8($sp) nop SW $a2, 12($sp) nop SW $s0, 16($sp) nop ADDIU $fp, $sp, 28  #store 1 in temp ADDIU
  //   $t1, $0, 1  #if (n < size && log_array[n] != 0)  #BGE $a0, $a2, if2 SLT $t6, $a0, $a2 BEQ $t6, $0,
  //   if2 nop  #creating offset for log_array SLL $t3, $a0, 2 ADDU $t3, $a1, $t3  #loading element in
  //   log_array[n] LW $t4, 0($t3) nop  BEQ $t4, $0, if2 nop  ADDIU $v0, $t4, 0  j epilogue nop  #if n == 1
  //   if2: nop  BNE $a0, $t1, else nop j epilogue nop  # if ((n % 2) == 0) else: nop  ADDIU $s0, $a0, 0
  //   SLL $t2, $a0, 31 BNE $t2, $0, inside_else nop SRA $a0, $a0, 1  jal fn nop  ADDIU $a0, $s0, 0  ADDIU
  //   $v0, $v0, 1  j last_if nop  inside_else: nop  ADDIU $s0, $a0, 0  #store argument in temp ADDIU $t0,
  //   $a0, 0  ADDU $a0, $a0, $t0 ADDU $a0, $a0, $t0 ADDIU $a0, $a0, 1  jal fn nop  ADDIU $a0, $s0, 0
  //   ADDIU $v0, $v0, 1  last_if: nop  #if n < size  #BGE $a0, $a2, epilogue SLT $t7, $a0, $a2 BEQ $t7,
  //   $0, epilogue  #creating offset for log_array SLL $t5, $a0, 2 ADDU $t5, $a1, $t5  #storing element in
  //   log_array[n] to register SW $v0, 0($t5) nop  epilogue: nop  LW $a0, 4($sp) nop LW $a1, 8($sp) nop LW
  //   $a2, 12($sp) nop LW $s0, 16($sp) nop LW $fp,        24($sp) nop LW $ra,     28($sp) nop ADDIU $sp,
  //   $sp, 32 jr $ra nop  exit:
  //   Mem Hazard A
  //   Ex Hazard B
  //   Mem Hazard B
  //   Ex Hazard A
  //   plus 8
endmodule

module Decode (
  input  [31:0] Inst,
  output [4:0] Destination,
  output [4:0] Shamt,
  output [5:0] Ctrl_Func,
  output [3:0] ALU_opCode,
  output [31:0] Imm,
  output [4:0] rS,
  output [4:0] rT,
  output WE,
  output [5:0] firstSix,
  output Store,
  output Load,
  output [3:0] sel,
  output instr_is_branch_or_jump,
  output [1:0] PCsel,
  output [25:0] target
);

  wire and_1_out, and_2_out, and_3_out, and_4_out, and_5_out, and_6_out, and_7_out, beq1bne_out,
       blez1bgtz_out, bltz1bgez_out, j_out, jr_out, not_1_out, not_2_out, not_3_out, not_4_out, not_5_out,
       not_6_out, not_7_out, not_8_out, not_9_out, not_10_out, not_11_out, not_12_out, not_13_out,
       not_14_out, not_15_out, not_16_out, not_17_out, not_18_out, not_19_out, not_20_out, not_21_out,
       not_22_out, not_23_out, not_24_out, not_25_out, not_26_out, not_27_out, not_28_out, not_29_out,
       not_30_out, not_31_out, not_32_out, not_33_out, not_34_out, not_35_out, not_36_out, not_37_out,
       not_38_out, not_39_out, not_40_out, not_41_out, not_43_out, or_1_out, or_3_out, st_out;
  wire [1:0] bit_extender_4_out, bit_extender_8_out, incrementer_1_p2, incrementer_2_p2, incrementer_3_p2,
       multiplexer_6_out, multiplexer_8_out;
  wire [3:0] bit_extender_2_out, bit_extender_3_out, multiplexer_2_out, multiplexer_9_out, not_44_out;
  wire [3:3] not_42_out;
  wire [4:0] bit_extender_1_out, multiplexer_3_out, multiplexer_4_out;
  wire [5:0] bit_extender_7_out, multiplexer_1_out;
  wire [31:0] bit_extender_5_out, bit_extender_6_out, bit_extender_9_out, multiplexer_10_out,
       multiplexer_13_out;

  not not_1 (not_1_out, Inst[28]);
  not not_2 (not_2_out, Inst[29]);
  not not_3 (not_3_out, Inst[30]);
  not not_4 (not_4_out, Inst[31]);
  and and_1 (and_1_out, Inst[26], Inst[27], not_1_out, not_2_out, not_3_out, not_4_out);
  not not_5 (not_5_out, Inst[30]);
  not not_6 (not_6_out, Inst[26]);
  not not_7 (not_7_out, Inst[28]);
  not not_8 (not_8_out, Inst[29]);
  not not_9 (not_9_out, Inst[30]);
  not not_10 (not_10_out, Inst[31]);
  not not_11 (not_11_out, Inst[27]);
  and beq1bne (beq1bne_out, not_11_out, Inst[28], not_12_out, not_13_out, not_14_out);
  not not_12 (not_12_out, Inst[29]);
  not not_13 (not_13_out, Inst[30]);
  not not_14 (not_14_out, Inst[31]);
  and blez1bgtz (blez1bgtz_out, Inst[27], Inst[28], not_15_out, not_16_out, not_17_out);
  not not_15 (not_15_out, Inst[29]);
  not not_16 (not_16_out, Inst[30]);
  not not_17 (not_17_out, Inst[31]);
  not not_18 (not_18_out, Inst[27]);
  not not_19 (not_19_out, Inst[28]);
  not not_20 (not_20_out, Inst[29]);
  not not_21 (not_21_out, Inst[30]);
  not not_22 (not_22_out, Inst[31]);
  not not_23 (not_23_out, Inst[26]);
  not not_24 (not_24_out, Inst[27]);
  not not_25 (not_25_out, Inst[28]);
  not not_26 (not_26_out, Inst[29]);
  not not_27 (not_27_out, Inst[30]);
  not not_28 (not_28_out, Inst[31]);
  not not_29 (not_29_out, Inst[0]);
  not not_30 (not_30_out, Inst[1]);
  not not_31 (not_31_out, Inst[2]);
  not not_32 (not_32_out, Inst[4]);
  not not_33 (not_33_out, Inst[5]);
  not not_34 (not_34_out, Inst[1]);
  not not_35 (not_35_out, Inst[2]);
  and and_2 (and_2_out, not_34_out, not_35_out, Inst[3], not_36_out, not_37_out);
  not not_36 (not_36_out, Inst[4]);
  not not_37 (not_37_out, Inst[5]);
  or or_1 (or_1_out, j_out, and_1_out);
  assign bit_extender_1_out = {{4{not_5_out}}, not_5_out};  // Bit_Extender bit_extender_1
  Multiplexer #(.width(6), .enable("false")) multiplexer_1 (
    .in0(Inst[5:0]), .in1(Inst[31:26]), .out(multiplexer_1_out), .sel(Inst[29]));
  and j (j_out, not_6_out, Inst[27], not_7_out, not_8_out, not_9_out, not_10_out);
  and bltz1bgez (bltz1bgez_out, Inst[26], not_18_out, not_19_out, not_20_out, not_21_out, not_22_out);
  and jr (jr_out, and_4_out, and_3_out);
  and and_3 (and_3_out, not_23_out, not_24_out, not_25_out, not_26_out, not_27_out, not_28_out);
  and and_4 (and_4_out, not_29_out, not_30_out, not_31_out, Inst[3], not_32_out, not_33_out);
  Multiplexer #(.width(4), .enable("false")) multiplexer_2 (
    .in0({Inst[2:0], Inst[31]}), .in1({Inst[28:26], Inst[31]}), .out(multiplexer_2_out), .sel(Inst[29]));
  and st (st_out, Inst[31], Inst[29]);
  and and_5 (and_5_out, and_2_out, and_3_out);
  Multiplexer #(.width(5), .enable("false")) multiplexer_3 (
    .in0(Inst[15:11]), .in1(Inst[20:16]), .out(multiplexer_3_out), .sel(Inst[29]));
  NotExactlyOne xnor_1 (
    .out(WE), .in0(blez1bgtz_out), .in1(j_out), .in2(beq1bne_out), .in3(jr_out), .in4(bltz1bgez_out),
    .in5(st_out));
  assign bit_extender_2_out = {{3{1'b0}}, Inst[31]};  // Bit_Extender bit_extender_2
  assign bit_extender_3_out = {{3{1'b1}}, Inst[31]};  // Bit_Extender bit_extender_3
  assign bit_extender_4_out = {{1{Inst[30]}}, Inst[30]};  // Bit_Extender bit_extender_4
  not not_38 (not_38_out, Inst[3]);
  not not_39 (not_39_out, Inst[5]);
  assign bit_extender_5_out = {{16{Inst[15]}}, Inst[15:0]};  // Bit_Extender bit_extender_5
  assign bit_extender_6_out = {{16{1'b0}}, Inst[15:0]};  // Bit_Extender bit_extender_6
  assign bit_extender_7_out = {{5{1'b0}}, Inst[31]};  // Bit_Extender bit_extender_7
  or or_2 (instr_is_branch_or_jump, or_1_out, beq1bne_out, blez1bgtz_out, bltz1bgez_out, and_5_out);
  or or_3 (or_3_out, blez1bgtz_out, bltz1bgez_out, beq1bne_out);
  Multiplexer #(.width(5), .enable("false")) multiplexer_4 (
    .in0(multiplexer_3_out), .in1(Inst[20:16]), .out(multiplexer_4_out), .sel(Load));
  not not_40 (not_40_out, Inst[2]);
  not not_41 (not_41_out, Inst[4]);
  not not_42 (not_42_out[3], bit_extender_7_out[3]);
  and and_6 (and_6_out, Inst[0], Inst[1], not_40_out, not_38_out, not_41_out, not_39_out);
  // Incrementer #(.width(2)) incrementer_1: pin names not known; wires that end beside it: bit_extender_4_out, incrementer_1_p2
  Multiplexer #(.width(5), .enable("false")) multiplexer_5 (
    .in0(multiplexer_4_out), .in1(bit_extender_1_out), .out(Destination), .sel(and_1_out));
  and and_7 (and_7_out, and_3_out, and_6_out);
  assign {not_44_out[3:2], bit_extender_8_out} = {{3{1'b0}}, Inst[31]};  // Bit_Extender bit_extender_8
  and and_8 (Store, Inst[31], Inst[29]);
  and and_9 (Load, Inst[31], not_43_out);
  not not_43 (not_43_out, Inst[29]);
  Multiplexer #(.width(2), .enable("false")) multiplexer_6 (
    .in0(bit_extender_4_out), .in1(incrementer_1_p2), .out(multiplexer_6_out), .sel(and_5_out));
  // Incrementer #(.width(2)) incrementer_2: pin names not known; wires that end beside it: incrementer_1_p2, incrementer_2_p2
  not not_44 (not_44_out[0], bit_extender_8_out[0]);
  not not_45 (not_44_out[1], bit_extender_8_out[1]);
  Multiplexer #(.width(4), .enable("false")) multiplexer_7 (
    .in0(bit_extender_2_out), .in1(bit_extender_3_out), .out(sel), .sel(Inst[26]));
  Multiplexer #(.width(2), .enable("false")) multiplexer_8 (
    .in0(multiplexer_6_out), .in1(incrementer_2_p2), .out(multiplexer_8_out), .sel(or_1_out));
  // Incrementer #(.width(2)) incrementer_3: pin names not known; wires that end beside it: incrementer_2_p2, incrementer_3_p2
  Multiplexer #(.width(4), .enable("false")) multiplexer_9 (
    .in0(multiplexer_2_out), .in1({Inst[3], Inst[1], Inst[2], Inst[0]}), .out(multiplexer_9_out),
    .sel(and_7_out));
  Multiplexer #(.width(32), .enable("false")) multiplexer_10 (
    .in0(bit_extender_5_out), .in1(bit_extender_6_out), .out(multiplexer_10_out), .sel(Inst[28]));
  Multiplexer #(.width(2), .enable("false")) multiplexer_11 (
    .in0(multiplexer_8_out), .in1(incrementer_3_p2), .out(PCsel), .sel(or_3_out));
  Multiplexer #(.width(6), .enable("false")) multiplexer_12 (
    .in0(multiplexer_1_out), .in1({bit_extender_7_out[5:4], not_42_out[3], bit_extender_7_out[2:0]}),
    .out(Ctrl_Func), .sel(Inst[31]));
  Multiplexer #(.width(32), .enable("false")) multiplexer_13 (
    .in0(multiplexer_10_out), .in1(bit_extender_5_out), .out(multiplexer_13_out), .sel(Inst[31]));
  Multiplexer #(.width(4), .enable("false")) multiplexer_14 (
    .in0(multiplexer_9_out), .in1(not_44_out), .out(ALU_opCode), .sel(Inst[31]));
  assign bit_extender_9_out = {{16{Inst[15]}}, Inst[15:0]};  // Bit_Extender bit_extender_9
  Multiplexer #(.width(32), .enable("false")) multiplexer_15 (
    .in0(multiplexer_13_out), .in1(bit_extender_9_out), .out(Imm), .sel(instr_is_branch_or_jump));

  assign firstSix = Inst[31:26];
  assign rS = Inst[25:21];
  assign rT = Inst[20:16];
  assign Shamt = Inst[10:6];
  assign target = Inst[25:0];
endmodule

module Execute (
  input  [4:0] Destination,
  input  [31:0] A,
  input  [31:0] B,
  input  [31:0] Imm,
  input  [4:0] Shamt,
  input  [5:0] Ctrl_Func,
  input  [3:0] ALU_opCode,
  input  [5:0] firstSix,
  input  WEin,
  output [4:0] RegDst,
  output [31:0] D,
  output WEout
);

  wire and_1_out, and_2_out, and_3_out, and_4_out, and_5_out, and_6_out, and_7_out, comparator_1_lt,
       comparator_2_lt, equals0_1_out_3, equals0_2_out_3, MOVN_out, MOVZ_out, multiplexer_6_out,
       multiplexer_7_out, not_2_out, not_3_out, not_4_out, not_5_out, not_6_out, not_7_out, not_8_out,
       not_9_out, not_10_out, not_11_out, not_12_out, not_13_out, not_14_out;
  wire [3:0] multiplexer_4_out, multiplexer_5_out;
  wire [3:3] not_1_out;
  wire [4:0] multiplexer_3_out;
  wire [31:0] bit_extender_1_out, bit_extender_2_out, bit_extender_3_out, leftshift16_1_out_3, mips_alu_1_p5,
       multiplexer_1_out, multiplexer_2_out, multiplexer_9_out, multiplexer_10_out;

  assign bit_extender_1_out = {{31{1'b0}}, firstSix[4]};  // Bit_Extender bit_extender_1
  assign bit_extender_2_out = {{26{1'b0}}, firstSix};  // Bit_Extender bit_extender_2
  not not_1 (not_1_out[3], ALU_opCode[3]);
  not not_2 (not_2_out, ALU_opCode[0]);
  Equals0 equals0_1 (.rt(bit_extender_2_out), .in_2(bit_extender_1_out), .out_3(equals0_1_out_3));
  not not_3 (not_3_out, Ctrl_Func[4]);
  not not_4 (not_4_out, Ctrl_Func[5]);
  Multiplexer #(.width(32), .enable("false")) multiplexer_1 (
    .in0(Imm), .in1(B), .out(multiplexer_1_out), .sel(Ctrl_Func[5]));
  and and_1 (and_1_out, not_2_out, ALU_opCode[1], ALU_opCode[2], ALU_opCode[3]);
  Equals0 equals0_2 (.rt(B), .in_2(bit_extender_1_out), .out_3(equals0_2_out_3));
  and and_2 (and_2_out, Ctrl_Func[0], Ctrl_Func[1], Ctrl_Func[2], Ctrl_Func[3], not_3_out, not_4_out);
  not not_5 (not_5_out, Ctrl_Func[2]);
  and and_3 (and_3_out, Ctrl_Func[1], not_5_out, Ctrl_Func[3], not_6_out, not_7_out);
  not not_6 (not_6_out, Ctrl_Func[4]);
  not not_7 (not_7_out, Ctrl_Func[5]);
  Multiplexer #(.width(32), .enable("false")) multiplexer_2 (
    .in0(B), .in1(Imm), .out(multiplexer_2_out), .sel(Ctrl_Func[3]));
  Multiplexer #(.width(5), .enable("false")) multiplexer_3 (
    .in0(Shamt), .in1(A[4:0]), .out(multiplexer_3_out), .sel(Ctrl_Func[2]));
  not not_8 (not_8_out, Ctrl_Func[3]);
  not not_9 (not_9_out, Ctrl_Func[4]);
  not not_10 (not_10_out, Ctrl_Func[5]);
  not not_11 (not_11_out, Ctrl_Func[0]);
  not not_12 (not_12_out, equals0_2_out_3);
  Multiplexer #(.width(4), .enable("false")) multiplexer_4 (
    .in0(ALU_opCode), .in1(multiplexer_5_out), .out(multiplexer_4_out), .sel(and_4_out));
  Multiplexer #(.width(4), .enable("false")) multiplexer_5 (
    .in0({not_1_out[3], ALU_opCode[2:0]}), .in1({ALU_opCode[0], ALU_opCode[1:0], ALU_opCode[1]}),
    .out(multiplexer_5_out), .sel(and_1_out));
  and and_4 (and_4_out, Ctrl_Func[2], and_5_out);
  and and_5 (and_5_out, Ctrl_Func[2], not_8_out, not_9_out, not_10_out);
  and MOVZ (MOVZ_out, not_11_out, equals0_2_out_3, and_3_out, equals0_1_out_3);
  and MOVN (MOVN_out, equals0_1_out_3, not_12_out, and_3_out, Ctrl_Func[0]);
  and and_6 (and_6_out, and_3_out, equals0_1_out_3);
  // Mips_ALU mips_alu_1: pin names not known; wires that end beside it: A, multiplexer_2_out, multiplexer_4_out, multiplexer_3_out, mips_alu_1_p5
  Multiplexer #(.enable("false")) multiplexer_6 (
    .in0(MOVZ_out), .in1(MOVN_out), .out(multiplexer_6_out), .sel(Ctrl_Func[0]));
  Comparator #(.width(32), .mode("unsigned")) comparator_1 (
    .a(A), .b(multiplexer_1_out), .lt(comparator_1_lt));  // open: gt, eq
  Comparator #(.width(32)) comparator_2 (.a(A), .b(multiplexer_1_out), .lt(comparator_2_lt));  // open: gt, eq
  not not_13 (not_13_out, Ctrl_Func[2]);
  not not_14 (not_14_out, Ctrl_Func[4]);
  Multiplexer #(.enable("false")) multiplexer_7 (
    .in0(comparator_2_lt), .in1(comparator_1_lt), .out(multiplexer_7_out), .sel(Ctrl_Func[0]));
  and and_7 (and_7_out, Ctrl_Func[1], not_13_out, Ctrl_Func[3], not_14_out);
  assign bit_extender_3_out = {{31{1'b0}}, multiplexer_7_out};  // Bit_Extender bit_extender_3
  Multiplexer #(.enable("false")) multiplexer_8 (.in0(WEin), .in1(multiplexer_6_out), .out(WEout), .sel(and_6_out));
  Multiplexer #(.width(32), .enable("false")) multiplexer_9 (
    .in0(mips_alu_1_p5), .in1(bit_extender_3_out), .out(multiplexer_9_out), .sel(and_7_out));
  LeftShift16 leftshift16_1 (.A(Imm), .out_3(leftshift16_1_out_3));  // open: in_2
  Multiplexer #(.width(32), .enable("false")) multiplexer_10 (
    .in0(multiplexer_9_out), .in1(A), .out(multiplexer_10_out), .sel(multiplexer_6_out));
  Multiplexer #(.width(32), .enable("false")) multiplexer_11 (
    .in0(multiplexer_10_out), .in1(leftshift16_1_out_3), .out(D), .sel(and_2_out));

  assign RegDst = Destination;

  // Notes on the sheet:
  //   Unsigned
  //   SIgned
endmodule

module AddressEquals (
  input  [4:0] A,
  input  [4:0] B,
  output out_3
);

  wire [4:0] xnor_1_out;

  assign xnor_1_out = ~(A ^ B);  // XNOR_Gate xnor_1, 5 bits wide
  and and_1 (out_3, xnor_1_out[0], xnor_1_out[1], xnor_1_out[2], xnor_1_out[3], xnor_1_out[4]);
endmodule

module WEequals0 (
  input  WE,
  input  in_2,
  output out_3
);

  and and_1 (out_3, WE, in_2);
endmodule

module RdEquals0 (
  input  [4:0] Rd,
  input  [4:0] in_2,
  output out_3
);

  wire [4:0] xnor_1_out;

  assign xnor_1_out = ~(Rd ^ in_2);  // XNOR_Gate xnor_1, 5 bits wide
  and and_1 (out_3, xnor_1_out[0], xnor_1_out[1], xnor_1_out[2], xnor_1_out[3], xnor_1_out[4]);
endmodule

module Equals0 (
  input  [31:0] rt,
  input  [31:0] in_2,
  output out_3
);

  wire [31:0] xnor_1_out;

  assign xnor_1_out = ~(rt ^ in_2);  // XNOR_Gate xnor_1, 32 bits wide
  and and_1 (out_3, xnor_1_out[0], xnor_1_out[1], xnor_1_out[2], xnor_1_out[3], xnor_1_out[4], xnor_1_out[5], xnor_1_out[6], xnor_1_out[7], xnor_1_out[8], xnor_1_out[9], xnor_1_out[10], xnor_1_out[11], xnor_1_out[12], xnor_1_out[13], xnor_1_out[14], xnor_1_out[15], xnor_1_out[16], xnor_1_out[17], xnor_1_out[18], xnor_1_out[19], xnor_1_out[20], xnor_1_out[21], xnor_1_out[22], xnor_1_out[23], xnor_1_out[24], xnor_1_out[25], xnor_1_out[26], xnor_1_out[27], xnor_1_out[28], xnor_1_out[29], xnor_1_out[30], xnor_1_out[31]);
endmodule

module LeftShift16 (
  input  [31:0] A,
  input  [15:0] in_2,
  output [31:0] out_3
);


  assign out_3 = {A[15:0], in_2};
endmodule

module oneHot (
  input  [1:0] in_1,
  output [3:0] out_2
);

  Decoder #(.select(2)) decoder_1 (
    .out0(out_2[0]), .out1(out_2[1]), .out2(out_2[2]), .out3(out_2[3]), .sel(in_1));  // open: en
endmodule

module LeftShift8 (
  input  [31:0] in_1,
  input  [7:0] in_2,
  output [31:0] out_3
);


  assign out_3 = {in_1[23:0], in_2};
endmodule

module LeftShift4 (
  input  [31:0] in_1,
  input  [3:0] in_2,
  output [31:0] out_3
);


  assign out_3 = {in_1[27:0], in_2};
endmodule

module LeftShift2 (
  input  [31:0] in_1,
  input  [1:0] in_2,
  output [31:0] out_3
);


  assign out_3 = {in_1[29:0], in_2};
endmodule

module LeftShift1 (
  input  [31:0] in_1,
  input  in_2,
  output [31:0] out_3
);


  assign out_3 = {in_1[30:0], in_2};
endmodule

module shiftMultiple (
  input  [31:0] in_1,
  input  [1:0] in_2,
  input  in_3,
  input  in_4,
  output [31:0] out_5
);

  wire [2:0] bit_extender_1_out;
  wire [30:0] bit_extender_2_out;
  wire [31:0] leftshift1_1_out_3, leftshift2_1_out_3, leftshift4_1_out_3, leftshift8_1_out_3,
       leftshift16_1_out_3, multiplexer_1_out, multiplexer_2_out, multiplexer_3_out, multiplexer_4_out;

  assign bit_extender_1_out = {{2{in_3}}, in_3};  // Bit_Extender bit_extender_1
  assign bit_extender_2_out = {{30{in_4}}, in_4};  // Bit_Extender bit_extender_2
  LeftShift16 leftshift16_1 (.A(in_1), .in_2(bit_extender_2_out[30:15]), .out_3(leftshift16_1_out_3));
  Multiplexer #(.width(32), .enable("false")) multiplexer_1 (
    .in0(in_1), .in1(leftshift16_1_out_3), .out(multiplexer_1_out), .sel(in_2[1]));
  LeftShift8 leftshift8_1 (.in_1(multiplexer_1_out), .in_2(bit_extender_2_out[14:7]), .out_3(leftshift8_1_out_3));
  Multiplexer #(.width(32), .enable("false")) multiplexer_2 (
    .in0(multiplexer_1_out), .in1(leftshift8_1_out_3), .out(multiplexer_2_out), .sel(in_2[0]));
  LeftShift4 leftshift4_1 (.in_1(multiplexer_2_out), .in_2(bit_extender_2_out[6:3]), .out_3(leftshift4_1_out_3));
  Multiplexer #(.width(32), .enable("false")) multiplexer_3 (
    .in0(multiplexer_2_out), .in1(leftshift4_1_out_3), .out(multiplexer_3_out), .sel(bit_extender_1_out[2]));
  Multiplexer #(.width(32), .enable("false")) multiplexer_4 (
    .in0(multiplexer_3_out), .in1(leftshift2_1_out_3), .out(multiplexer_4_out), .sel(bit_extender_1_out[1]));
  LeftShift2 leftshift2_1 (.in_1(multiplexer_3_out), .in_2(bit_extender_2_out[2:1]), .out_3(leftshift2_1_out_3));
  LeftShift1 leftshift1_1 (.in_1(multiplexer_4_out), .in_2(bit_extender_2_out[0]), .out_3(leftshift1_1_out_3));
  Multiplexer #(.width(32), .enable("false")) multiplexer_5 (
    .in0(multiplexer_4_out), .in1(leftshift1_1_out_3), .out(out_5), .sel(bit_extender_1_out[0]));
endmodule

module branchYes (
  input  [31:0] A,
  input  [31:0] B,
  input  [5:0] firstSix,
  input  [4:0] rt,
  output out_5
);

  wire and_1_out, and_2_out, and_3_out, and_4_out, and_5_out, comparator_1_eq, comparator_2_eq,
       comparator_2_gt, comparator_2_lt, multiplexer_1_out, multiplexer_2_out, multiplexer_3_out,
       multiplexer_4_out, not_1_out, not_2_out, not_3_out, not_4_out, not_5_out, not_6_out, or_1_out,
       or_2_out;
  wire [31:0] bit_extender_1_out;

  assign bit_extender_1_out = {{31{1'b0}}, firstSix[4]};  // Bit_Extender bit_extender_1
  Comparator #(.width(32)) comparator_1 (.a(A), .b(B), .eq(comparator_1_eq));  // open: gt, lt
  Comparator #(.width(32)) comparator_2 (
    .a(A), .b(bit_extender_1_out), .gt(comparator_2_gt), .eq(comparator_2_eq), .lt(comparator_2_lt));
  or or_1 (or_1_out, comparator_2_gt, comparator_2_eq);
  and and_1 (and_1_out, firstSix[0], not_1_out, not_2_out);
  not not_1 (not_1_out, firstSix[1]);
  not not_2 (not_2_out, firstSix[2]);
  not not_3 (not_3_out, firstSix[1]);
  and and_2 (and_2_out, comparator_1_eq, firstSix[2], not_3_out);
  not not_4 (not_4_out, comparator_1_eq);
  and and_3 (and_3_out, not_4_out, firstSix[2], not_3_out);
  or or_2 (or_2_out, comparator_2_eq, comparator_2_lt);
  and and_4 (and_4_out, or_1_out, and_1_out);
  Multiplexer #(.enable("false")) multiplexer_1 (
    .in0(and_2_out), .in1(and_3_out), .out(multiplexer_1_out), .sel(firstSix[0]));
  and and_5 (and_5_out, or_2_out, firstSix[2], firstSix[1]);
  not not_5 (not_5_out, and_5_out);
  not not_6 (not_6_out, and_4_out);
  Multiplexer #(.enable("false")) multiplexer_2 (
    .in0(not_6_out), .in1(and_4_out), .out(multiplexer_2_out), .sel(rt[0]));
  Multiplexer #(.enable("false")) multiplexer_3 (
    .in0(multiplexer_1_out), .in1(multiplexer_4_out), .out(multiplexer_3_out), .sel(firstSix[1]));
  Multiplexer #(.enable("false")) multiplexer_4 (
    .in0(and_5_out), .in1(not_5_out), .out(multiplexer_4_out), .sel(firstSix[0]));
  Multiplexer #(.enable("false")) multiplexer_5 (
    .in0(multiplexer_2_out), .in1(multiplexer_3_out), .out(out_5), .sel(firstSix[2]));
endmodule

module stall (
  input  load,
  input  [4:0] rs,
  input  [4:0] rt,
  input  [4:0] rdNext,
  output stall
);

  wire addressequals_1_out_3, addressequals_2_out_3, and_1_out, and_2_out;

  AddressEquals addressequals_1 (.A(rs), .B(rdNext), .out_3(addressequals_1_out_3));
  AddressEquals addressequals_2 (.A(rt), .B(rdNext), .out_3(addressequals_2_out_3));
  and and_1 (and_1_out, load, addressequals_1_out_3);
  and and_2 (and_2_out, load, addressequals_2_out_3);
  or or_1 (stall, and_1_out, and_2_out);
endmodule
